# Fritzing sketch drawingbot (saved by Fritzing 0.9.3b)

parts:
  Part1 = Arduino Uno (Rev3) - ICSP
  X1 = X113647 Stepper Driver Board [package=board]
  X2 = X113647 Stepper Driver Board [package=board]
  J1 = female alternating pin header, 9 pins [form="♀ (female)"]
  J2 = female alternating pin header, 1 pin [form="♀ (female)"]
  SERVO1 = Tower Pro SG90 servo [part_number=101246]

nets:
  N1: Part1.5V, J1.pin7
  N2: Part1.ICSP_MOSI, Part1.D11_PWM/MOSI, X2.IN4
  N3: Part1.GND, J1.pin6
  N4: Part1.D8, X2.IN1
  N5: Part1.D9_PWM, X2.IN2
  N6: Part1.D10_PWM/SS, X2.IN3
  N7: Part1.D2, X1.IN1
  N8: Part1.D3_PWM, X1.IN2
  N9: Part1.D4, X1.IN3
  N10: Part1.D5_PWM, X1.IN4
  N11: Part1.D7, J2.pin1
  N12: X1.GND, J1.pin4
  N13: X1.+V, J1.pin9
  N14: X2.GND, J1.pin5
  N15: X2.+V, J1.pin8
  N16: J1.pin1, SERVO1.Signal
  N17: J1.pin2, SERVO1.+5V
  N18: J1.pin3, SERVO1.GND

notes:
  D + - - - - + + +
  D

custom parts:
  X113647 Stepper Driver Board: A common stepper motor driver board based on ULN2003APG darlington array
  Tower Pro SG90 servo: Original file by John De Cristofaro http://www.adafruit.com/products/1449 Adafruit Feedback Servo (Small) Edited by: e-radionica.com 28/9/2015
